# Fritzing sketch Board2simple (saved by Fritzing 0.9.2b)
circuit board: 6.88566cm x 5.36311cm
breadboards: 4

parts:
  PCB1 = Arduino Shield PCB  # not connected
  Arduino1 = Arduino Uno (Rev3)
  S1 = Pushbutton [package="[THT]"]
  LED1 = LED - 5mm [color="Green (555nm)" package="5 mm [THT]"]
  R1 = Resistor [tolerance=±5% resistance=470 package=THT]
  S2 = Pushbutton [package="[THT]"]
  R2 = Resistor [tolerance=±5% resistance=470 package=THT]
  LED2 = LED - 5mm [color="Green (555nm)" package="5 mm [THT]"]
  S3 = Pushbutton [package="[THT]"]
  R3 = Resistor [tolerance=±5% resistance=470 package=THT]
  LED3 = LED - 5mm [color="Green (555nm)" package="5 mm [THT]"]
  S4 = Pushbutton [package="[THT]"]
  R4 = Resistor [tolerance=±5% resistance=470 package=THT]
  LED4 = LED - 5mm [color="Green (555nm)" package="5 mm [THT]"]
  S5 = Pushbutton [package="[THT]"]
  R5 = Resistor [tolerance=±5% resistance=470 package=THT]
  LED5 = LED - 5mm [color="Green (555nm)" package="5 mm [THT]"]
  S6 = Pushbutton [package="[THT]"]
  R6 = Resistor [tolerance=±5% resistance=470 package=THT]
  LED6 = LED - 5mm [color="Green (555nm)" package="5 mm [THT]"]
  S7 = Pushbutton [package="[THT]"]
  S8 = Pushbutton [package="[THT]"]
  S9 = Pushbutton [package="[THT]"]
  S10 = Pushbutton [package="[THT]"]
  S11 = Pushbutton [package="[THT]"]
  S12 = Pushbutton [package="[THT]"]
  R7 = Resistor [tolerance=±5% resistance=470 package=THT]
  R8 = Resistor [tolerance=±5% resistance=470 package=THT]
  R9 = Resistor [tolerance=±5% resistance=470 package=THT]
  R10 = Resistor [tolerance=±5% resistance=470 package=THT]
  R11 = Resistor [tolerance=±5% resistance=470 package=THT]
  R12 = Resistor [tolerance=±5% resistance=470 package=THT]
  LED7 = LED - 5mm [color="Green (555nm)" package="5 mm [THT]"]
  LED8 = LED - 5mm [color="Green (555nm)" package="5 mm [THT]"]
  LED9 = LED - 5mm [color="Green (555nm)" package="5 mm [THT]"]
  LED10 = LED - 5mm [color="Green (555nm)" package="5 mm [THT]"]
  LED11 = LED - 5mm [color="Green (555nm)" package="5 mm [THT]"]
  LED12 = LED - 5mm [color="Green (555nm)" package="5 mm [THT]"]
  S13 = Pushbutton [package="[THT]"]
  R13 = Resistor [tolerance=±5% resistance=470 package=THT]
  LED13 = LED - 5mm [color="Green (555nm)" package="5 mm [THT]"]
  R14 = Rotary Potentiometer (Small) [maximum_resistance=100kΩ package=THT]
  S14 = Pushbutton [package="[THT]"]
  R15 = Resistor [tolerance=±5% resistance=470 package=THT]
  LED14 = LED - 5mm [color="Blue (430nm)" package="5 mm [THT]"]
  S15 = Pushbutton [package="[THT]"]
  R16 = Resistor [tolerance=±5% resistance=470 package=THT]
  R17 = Rotary Potentiometer (Small) [maximum_resistance=100kΩ package=THT]
  LED15 = LED - 5mm [color="Blue (430nm)" package="5 mm [THT]"]
  S16 = Pushbutton [package="[THT]"]
  R18 = Resistor [tolerance=±5% resistance=470 package=THT]
  R19 = Rotary Potentiometer (Small) [maximum_resistance=100kΩ package=THT]
  LED16 = LED - 5mm [color="Blue (430nm)" package="5 mm [THT]"]
  S17 = Pushbutton [package="[THT]"]
  S18 = Pushbutton [package="[THT]"]
  S19 = Pushbutton [package="[THT]"]
  R20 = Resistor [tolerance=±5% resistance=470 package=THT]
  R21 = Resistor [tolerance=±5% resistance=470 package=THT]
  R22 = Resistor [tolerance=±5% resistance=470 package=THT]
  R23 = Rotary Potentiometer (Small) [maximum_resistance=100kΩ package=THT]
  R24 = Rotary Potentiometer (Small) [maximum_resistance=100kΩ package=THT]
  R25 = Rotary Potentiometer (Small) [maximum_resistance=100kΩ package=THT]
  LED17 = LED - 5mm [color="Blue (430nm)" package="5 mm [THT]"]
  LED18 = LED - 5mm [color="Blue (430nm)" package="5 mm [THT]"]
  LED19 = LED - 5mm [color="Blue (430nm)" package="5 mm [THT]"]

nets (from the breadboard view):
  N1: Arduino1.A0, Arduino1.A1, Arduino1.A2, Arduino1.A3, Arduino1.A4/SDA, Arduino1.A5/SCL, Arduino1.D8, Arduino1.D9_PWM, Arduino1.D10_PWM/SS, Arduino1.D11_PWM/MOSI, Arduino1.D12/MISO, Arduino1.D13/SCK, Arduino1.D1/TX, Arduino1.D2, Arduino1.D3_PWM, Arduino1.D4, Arduino1.D5_PWM, Arduino1.D6_PWM, Arduino1.D7, S1.Pin_3, S1.Pin_4, R1.Pin_0, S2.Pin_3, S2.Pin_4, R2.Pin_0, S3.Pin_3, S3.Pin_4, R3.Pin_0, S4.Pin_3, S4.Pin_4, R4.Pin_0, S5.Pin_3, S5.Pin_4, R5.Pin_0, S6.Pin_3, S6.Pin_4, R6.Pin_0, S7.Pin_3, S7.Pin_4, S8.Pin_3, S8.Pin_4, S9.Pin_3, S9.Pin_4, S10.Pin_3, S10.Pin_4, S11.Pin_3, S11.Pin_4, S12.Pin_3, S12.Pin_4, R7.Pin_0, R8.Pin_0, R9.Pin_0, R10.Pin_0, R11.Pin_0, R12.Pin_0, S13.Pin_3, S13.Pin_4, R13.Pin_0, R14.wiper, R14.leg2, S14.Pin_1, S14.Pin_2, R15.Pin_1, S15.Pin_1, S15.Pin_2, R16.Pin_1, R17.wiper, R17.leg2, S16.Pin_1, S16.Pin_2, R18.Pin_1, R19.wiper, R19.leg2, S17.Pin_1, S17.Pin_2, S18.Pin_1, S18.Pin_2, S19.Pin_1, S19.Pin_2, R20.Pin_1, R21.Pin_1, R22.Pin_1, R23.wiper, R23.leg2, R24.wiper, R24.leg2, R25.wiper, R25.leg2
  N2: Arduino1.GND, LED1.cathode, LED2.cathode, LED3.cathode, LED4.cathode, LED5.cathode, LED6.cathode, LED7.cathode, LED8.cathode, LED9.cathode, LED10.cathode, LED11.cathode, LED12.cathode, LED13.cathode, R14.leg1, LED14.cathode, LED15.cathode, R19.leg1, LED16.cathode, R23.leg1, R25.leg1, LED17.cathode, LED18.cathode, LED19.cathode
  N3: S1.Pin_1, S1.Pin_2
  N4: LED1.anode, R1.Pin_1
  N5: S2.Pin_1, S2.Pin_2
  N6: R2.Pin_1, LED2.anode
  N7: S3.Pin_1, S3.Pin_2
  N8: R3.Pin_1, LED3.anode
  N9: S4.Pin_1, S4.Pin_2
  N10: R4.Pin_1, LED4.anode
  N11: S5.Pin_1, S5.Pin_2
  N12: R5.Pin_1, LED5.anode
  N13: S6.Pin_1, S6.Pin_2
  N14: R6.Pin_1, LED6.anode
  N15: S7.Pin_1, S7.Pin_2
  N16: S8.Pin_1, S8.Pin_2
  N17: S9.Pin_1, S9.Pin_2
  N18: S10.Pin_1, S10.Pin_2
  N19: S11.Pin_1, S11.Pin_2
  N20: S12.Pin_1, S12.Pin_2
  N21: R7.Pin_1, LED9.anode
  N22: R8.Pin_1, LED11.anode
  N23: R9.Pin_1, LED7.anode
  N24: R10.Pin_1, LED8.anode
  N25: R11.Pin_1, LED10.anode
  N26: R12.Pin_1, LED12.anode
  N27: S13.Pin_1, S13.Pin_2
  N28: R13.Pin_1, LED13.anode
  N29: S14.Pin_3, S14.Pin_4
  N30: R15.Pin_0, LED14.anode
  N31: S15.Pin_3, S15.Pin_4
  N32: R16.Pin_0, LED15.anode
  N33: S16.Pin_3, S16.Pin_4
  N34: R18.Pin_0, LED16.anode
  N35: S17.Pin_3, S17.Pin_4
  N36: S18.Pin_3, S18.Pin_4
  N37: S19.Pin_3, S19.Pin_4
  N38: R20.Pin_0, LED17.anode
  N39: R21.Pin_0, LED18.anode
  N40: R22.Pin_0, LED19.anode

custom parts:
  Arduino Shield PCB: Plain PCB Shaped to fit an Arduino "Shield"
