# Fritzing sketch DIOTestPCB (saved by Fritzing 0.9.2b)
breadboards: 1

parts:
  R9 = Resistor [tolerance=±5% resistance=220 package=THT]
  R10 = Resistor [tolerance=±5% resistance=220 package=THT]
  LED9 = LED - 5mm [color="Red (633nm)" package="5 mm [THT]"]
  LED10 = LED - 5mm [color="Red (633nm)" package="5 mm [THT]"]
  JP1 = FTDI_BASIC [package=ftdi_basic]
  JP2 = FTDI_BASIC [package=ftdi_basic]
  R14 = Resistor [tolerance=±5% resistance=220 package=THT]  # not connected
  R15 = Resistor [tolerance=±5% resistance=220 package=THT]
  R16 = Resistor [tolerance=±5% resistance=220 package=THT]
  LED15 = LED - 5mm [color="Red (633nm)" package="5 mm [THT]"]
  LED16 = LED - 5mm [color="Red (633nm)" package="5 mm [THT]"]
  R17 = Resistor [tolerance=±5% resistance=220 package=THT]
  R18 = Resistor [tolerance=±5% resistance=220 package=THT]
  LED17 = LED - 5mm [color="Red (633nm)" package="5 mm [THT]"]
  LED18 = LED - 5mm [color="Red (633nm)" package="5 mm [THT]"]
  R19 = Resistor [tolerance=±5% resistance=220 package=THT]
  R20 = Resistor [tolerance=±5% resistance=220 package=THT]
  LED19 = LED - 5mm [color="Red (633nm)" package="5 mm [THT]"]
  LED20 = LED - 5mm [color="Red (633nm)" package="5 mm [THT]"]
  R21 = Resistor [tolerance=±5% resistance=220 package=THT]
  R22 = Resistor [tolerance=±5% resistance=220 package=THT]
  LED21 = LED - 5mm [color="Red (633nm)" package="5 mm [THT]"]
  LED22 = LED - 5mm [color="Red (633nm)" package="5 mm [THT]"]
  R23 = Resistor [tolerance=±5% resistance=220 package=THT]
  R24 = Resistor [tolerance=±5% resistance=220 package=THT]
  LED23 = LED - 5mm [color="Red (633nm)" package="5 mm [THT]"]
  LED24 = LED - 5mm [color="Red (633nm)" package="5 mm [THT]"]

nets:
  N1: R9.Pin_0, LED10.cathode, JP1.4
  N2: R9.Pin_1, LED9.anode
  N3: R10.Pin_0, LED9.cathode, JP2.5
  N4: R10.Pin_1, LED10.anode
  N5: JP1.5, R23.Pin_0, LED24.cathode
  N6: JP1.1, R21.Pin_0, LED22.cathode
  N7: JP1.6, R19.Pin_0, LED20.cathode
  N8: JP1.2, R17.Pin_0, LED18.cathode
  N9: JP1.3, R15.Pin_0, LED16.cathode
  N10: JP2.1, R16.Pin_0, LED15.cathode
  N11: JP2.6, R18.Pin_0, LED17.cathode
  N12: JP2.2, R20.Pin_0, LED19.cathode
  N13: JP2.3, R22.Pin_0, LED21.cathode
  N14: JP2.4, R24.Pin_0, LED23.cathode
  N15: R15.Pin_1, LED15.anode
  N16: R16.Pin_1, LED16.anode
  N17: R17.Pin_1, LED17.anode
  N18: R18.Pin_1, LED18.anode
  N19: R19.Pin_1, LED19.anode
  N20: R20.Pin_1, LED20.anode
  N21: R21.Pin_1, LED21.anode
  N22: R22.Pin_1, LED22.anode
  N23: R23.Pin_1, LED23.anode
  N24: R24.Pin_1, LED24.anode
